# Fritzing sketch Breadboard_Circuit (saved by Fritzing 0.9.5d)
breadboards: 1

parts:
  U1 = NodeMCU V3.0
  Part1 = Adafruit Micro USB Breakout [part_number="Adafruit #1833"]
  J1 = screw terminal, 3 pins
  U2 = WS2812 RGB LED strip

nets:
  N1: U1.D3, J1.pin2, U2.DIN
  GND: U1.GND#6, U1.GND#13, U1.GND#16, U1.GND#33, Part1.GND, J1.pin1, U2.GND
  VIN: U1.Vin, Part1.VBUS, J1.pin3, U2.VCC

custom parts:
  NodeMCU V3.0: ESP8266 based NodeMCU
  Adafruit Micro USB Breakout: Simple but effective - this breakout board has a USB Micro-B connector, with all 5 pins broken out. Great for pairing with a microcontroller with USB support, or adding USB 5V power to a project. We use a micro-AB connector with through-hole shielding pads for an excellent strong connection - it won't rip off by accident! Comes with one fully assembled and tested micro B breakout PCB and a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
  WS2812 RGB LED strip: WS2812 strip
