# Fritzing sketch Light Controller (saved by Fritzing 0.9.3b)
circuit board: 2.6cm x 5cm
breadboards: 1

parts:
  U1 = NodeMCU V3.0
  J1 = screw terminal, 3 pins
  J2 = female pin header, 5 pins [form="♀ (female)"]

nets:
  N1: U1.D3, J1.pin2
  N2: U1.GND#6, U1.GND#13, U1.GND#16, U1.GND#33, J1.pin3, J2.pin5
  N3: U1.Vin, J1.pin1, J2.pin1

notes:
  uzair ahmed

custom parts:
  NodeMCU V3.0: ESP8266 based NodeMCU
