# Fritzing sketch LightController_Final (saved by Fritzing 0.9.3b)
circuit board: 2.71817cm x 4.99125cm
breadboards: 1

parts:
  J1 = screw terminal, 3 pins
  J2 = female pin header, 5 pins [form="♀ (female)"]
  J3 = female pin header, 15 pins [form="♀ (female)"]  # not connected
  J4 = female pin header, 15 pins [form="♀ (female)"]  # not connected

nets:
  N1: J1.pin1, J2.pin1
  N2: J1.pin3, J2.pin5

notes:
  uzair ahmed
