# Fritzing sketch Perfboard_Circuit (saved by Fritzing 0.9.5d)
perfboards: 1

parts:
  U1 = NodeMCU V3.0
  U2 = WS2812 RGB LED strip
  Part1 = Adafruit Micro USB Breakout [part_number="Adafruit #1833"]
  J1 = screw terminal, 3 pins
  JP1 = M16 [package=1x16_machine-pin-header_lock.004]
  JP2 = M16 [package=1x16_machine-pin-header_lock.004]

nets:
  N1: U1.D0, JP2.15
  N2: U1.D1, JP2.14
  N3: U1.D2, JP2.13
  N4: U1.D3, U2.DIN, J1.pin2, JP2.12
  N5: U1.D4, JP2.11
  N6: U1.3V3, JP1.5, JP2.1, JP2.10
  GND: U1.GND#6, U1.GND#13, U1.GND#16, U1.GND#33, U2.GND, Part1.GND, J1.pin1, JP1.2, JP1.6, JP2.2, JP2.9
  N7: U1.D5, JP2.8
  N8: U1.D6, JP2.7
  N9: U1.D7, JP2.6
  N10: U1.D8, JP2.5
  N11: U1.RX, JP2.4
  N12: U1.TX, JP2.3
  VIN: U1.Vin, U2.VCC, Part1.VBUS, J1.pin3, JP1.1
  N13: U1.RST, JP1.3
  N14: U1.EN, JP1.4
  N15: U1.SK, JP1.7
  N16: U1.S0, JP1.8
  N17: U1.SC, JP1.9
  N18: U1.S1, JP1.10
  N19: U1.S2, JP1.11
  N20: U1.S3, JP1.12
  N21: U1.VU, JP1.13
  N22: U1.GND#41, JP1.14
  N23: U1.A0, JP1.15

custom parts:
  NodeMCU V3.0: ESP8266 based NodeMCU
  WS2812 RGB LED strip: WS2812 strip
  Adafruit Micro USB Breakout: Simple but effective - this breakout board has a USB Micro-B connector, with all 5 pins broken out. Great for pairing with a microcontroller with USB support, or adding USB 5V power to a project. We use a micro-AB connector with through-hole shielding pads for an excellent strong connection - it won't rip off by accident! Comes with one fully assembled and tested micro B breakout PCB and a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
